# Fritzing sketch crabdle_schematic (saved by Fritzing 0.9.3b)

parts:
  U1 = LIPO-1000mAh [package=lipo-1000]
  IcezumAlhambra = iceZUM Alhambra  # not connected
  U2 = LIPO-1000mAh [package=lipo-1000]
  J1 = Basic Servo  # not connected
  J2 = Basic Servo  # not connected
  J3 = Basic Servo  # not connected
  Raspberry_Pi_1 = Raspberry Pi 3 [part_number=RPI-3-V1.2]
  U3 = Mini-360 DC-DC Buck converter [package=THT]
  M1 = DC-DC Power Module (3.3V)  # not connected

nets:
  N1: U1.+, U2.-
  N2: U1.-, U3.IN-
  N3: U2.+, U3.IN+
  N4: Raspberry_Pi_1.GND, U3.OUT-
  N5: Raspberry_Pi_1.5V, U3.OUT+

custom parts:
  iceZUM Alhambra: Arduino/zum compatible Open FPGA electronic board. Synthesize hardware easily, using only open source tools
  Mini-360 DC-DC Buck converter: Mini-360 DC-DC Buck converter. Tiny buck step down voltage converter, input voltage 4.75 to 23V output 1 to 17V adjustable. Available from ebay and the like.
  DC-DC Power Module (3.3V): YP 46 DC-DC Power Module based con AMS1117-3.3 Input: DC 6~12V (input power must higher 1V than output power); Output: 3.3 (+/-0.05V error), 800mA
