# Fritzing sketch doodle_schematic (saved by Fritzing 0.9.3b)

parts:
  MCU1 = Raspberry Pi Zero
  U1 = LIPO-1000mAh [package=lipo-1000]
  IcezumAlhambra = iceZUM Alhambra
  U2 = LIPO-1000mAh [package=lipo-1000]
  M1 = fc-51 [package=THT]
  M2 = fc-51 [package=THT]
  J1 = Basic Servo  # not connected
  J2 = Basic Servo  # not connected
  J3 = Basic Servo  # not connected

nets:
  N1: MCU1.pin_2, IcezumAlhambra.5V
  N2: MCU1.pin_6, IcezumAlhambra.GND, U2.-
  N3: U1.+, IcezumAlhambra.VIN
  N4: U1.-, U2.+
  N5: IcezumAlhambra.D6, IcezumAlhambra.V6#53, M1.pin1
  N6: IcezumAlhambra.G8, IcezumAlhambra.G7, IcezumAlhambra.G6, M1.pin2, M2.pin2
  N7: IcezumAlhambra.V9, IcezumAlhambra.V7#38, IcezumAlhambra.V6#39, M1.pin3, M2.pin3
  N8: IcezumAlhambra.V7#52, M2.pin1

custom parts:
  iceZUM Alhambra: Arduino/zum compatible Open FPGA electronic board. Synthesize hardware easily, using only open source tools
